# Fritzing sketch Project Schematics (saved by Fritzing 0.8.7b)
breadboards: 2

parts:
  PROJECT_Digital_and_Binary_Clock_With_LEDs_(Schematics) = Arduino Uno (Rev3)
  Shift_Register_1 = 74HC595 SMD [package="SO16 [SMD]"]
  Shift_Register_2 = 74HC595 SMD [package="SO16 [SMD]"]
  Shift_Register_3 = 74HC595 SMD [package="SO16 [SMD]"]
  LCD1 = LCD screen
  R1 = Resistor [tolerance=±5% resistance=1k package=THT]
  S1 = Pushbutton [package="[THT]"]
  S2 = Pushbutton [package="[THT]"]
  LED2 = LED - 5mm [color="Blue (430nm)" package="5 mm [THT]"]
  LED3 = LED - 5mm [color="Blue (430nm)" package="5 mm [THT]"]
  LED4 = LED - 5mm [color="Blue (430nm)" package="5 mm [THT]"]
  LED5 = LED - 5mm [color="Blue (430nm)" package="5 mm [THT]"]
  LED6 = LED - 5mm [color="Green (555nm)" package="5 mm [THT]"]
  LED7 = LED - 5mm [color="Red (633nm)" package="5 mm [THT]"]
  LED8 = LED - 5mm [color="Red (633nm)" package="5 mm [THT]"]
  LED9 = LED - 5mm [color="Red (633nm)" package="5 mm [THT]"]
  LED10 = LED - 5mm [color="Red (633nm)" package="5 mm [THT]"]
  LED11 = LED - 5mm [color="Red (633nm)" package="5 mm [THT]"]
  LED12 = LED - 5mm [color="Red (633nm)" package="5 mm [THT]"]
  LED13 = LED - 5mm [color="Green (555nm)" package="5 mm [THT]"]
  LED14 = LED - 5mm [color="Yellow (585nm)" package="5 mm [THT]"]
  LED17 = LED - 5mm [color="Yellow (585nm)" package="5 mm [THT]"]
  LED18 = LED - 5mm [color="Yellow (585nm)" package="5 mm [THT]"]
  S3 = Pushbutton [package="[THT]"]
  R2 = Resistor [tolerance=±5% resistance=1k package=THT]
  R3 = Resistor [tolerance=±5% resistance=1k package=THT]
  R4 = Resistor [tolerance=±5% resistance=1k package=THT]
  LED19 = LED - 5mm [color="Yellow (585nm)" package="5 mm [THT]"]
  R5 = Resistor [tolerance=±5% resistance=1k package=THT]
  LED1 = LED - 5mm [color="Blue (430nm)" package="5 mm [THT]"]
  R6 = Resistor [tolerance=±5% resistance=1k package=THT]
  R7 = Resistor [tolerance=±5% resistance=1k package=THT]
  R8 = Resistor [tolerance=±5% resistance=1k package=THT]
  R9 = Resistor [tolerance=±5% resistance=1k package=THT]
  R10 = Resistor [tolerance=±5% resistance=1k package=THT]
  R11 = Resistor [tolerance=±5% resistance=1k package=THT]
  R12 = Resistor [tolerance=±5% resistance=1k package=THT]
  R13 = Resistor [tolerance=±5% resistance=1k package=THT]
  R14 = Resistor [tolerance=±5% resistance=1k package=THT]
  R15 = Resistor [tolerance=±5% resistance=1k package=THT]
  R16 = Resistor [tolerance=±5% resistance=1k package=THT]
  R17 = Resistor [tolerance=±5% resistance=1k package=THT]
  R18 = Resistor [tolerance=±5% resistance=1k package=THT]
  R19 = Resistor [tolerance=±5% resistance=1k package=THT]
  LED15 = LED - 5mm [color="Yellow (585nm)" package="5 mm [THT]"]
  LED16 = LED - 5mm [color="Yellow (585nm)" package="5 mm [THT]"]
  R20 = Resistor [tolerance=±5% resistance=1k package=THT]
  R21 = Resistor [tolerance=±5% resistance=1k package=THT]
  R22 = Resistor [tolerance=±5% resistance=1k package=THT]
  R23 = Resistor [tolerance=±5% resistance=1k package=THT]
  J1 = Piezo Speaker
  POT = Rotary Potentiometer (Small) [maximum_resistance=1kΩ package=THT]
  R24 = Resistor [tolerance=±5% resistance=1M package=THT]

nets (from the schematic view):
  N1: PROJECT_Digital_and_Binary_Clock_With_LEDs_(Schematics).A0, R24.Pin_0
  N2: PROJECT_Digital_and_Binary_Clock_With_LEDs_(Schematics).D8, LCD1.DB7
  N3: PROJECT_Digital_and_Binary_Clock_With_LEDs_(Schematics).D9_PWM, LCD1.DB6
  N4: PROJECT_Digital_and_Binary_Clock_With_LEDs_(Schematics).D10_PWM/SS, LCD1.DB5
  N5: PROJECT_Digital_and_Binary_Clock_With_LEDs_(Schematics).D11_PWM/MOSI, LCD1.DB4
  N6: PROJECT_Digital_and_Binary_Clock_With_LEDs_(Schematics).D12/MISO, LCD1.E
  N7: PROJECT_Digital_and_Binary_Clock_With_LEDs_(Schematics).D13/SCK, LCD1.RS
  GND: PROJECT_Digital_and_Binary_Clock_With_LEDs_(Schematics).GND, Shift_Register_1.GND, Shift_Register_1.OE, Shift_Register_2.GND, Shift_Register_2.OE, Shift_Register_3.GND, Shift_Register_3.OE, LCD1.VSS, LCD1.R/W, LCD1.LED-, LED2.cathode, LED3.cathode, LED4.cathode, LED5.cathode, LED6.cathode, LED7.cathode, LED8.cathode, LED9.cathode, LED10.cathode, LED11.cathode, LED12.cathode, LED13.cathode, LED14.cathode, LED17.cathode, LED18.cathode, R2.Pin_0, R3.Pin_0, R4.Pin_0, LED19.cathode, LED1.cathode, LED15.cathode, LED16.cathode, J1.pin1, POT.leg2
  N8: PROJECT_Digital_and_Binary_Clock_With_LEDs_(Schematics).D2, Shift_Register_1.SH_CP, Shift_Register_2.SH_CP, Shift_Register_3.SH_CP
  N9: PROJECT_Digital_and_Binary_Clock_With_LEDs_(Schematics).D3_PWM, Shift_Register_1.ST_CP, Shift_Register_2.ST_CP, Shift_Register_3.ST_CP
  N10: PROJECT_Digital_and_Binary_Clock_With_LEDs_(Schematics).D4, Shift_Register_1.DS
  N11: PROJECT_Digital_and_Binary_Clock_With_LEDs_(Schematics).D5_PWM, S1.Pin_3, S1.Pin_4, R2.Pin_1
  N12: PROJECT_Digital_and_Binary_Clock_With_LEDs_(Schematics).D6_PWM, S2.Pin_3, S2.Pin_4, R3.Pin_1
  N13: PROJECT_Digital_and_Binary_Clock_With_LEDs_(Schematics).D7, S3.Pin_3, S3.Pin_4, R4.Pin_1
  VCC: PROJECT_Digital_and_Binary_Clock_With_LEDs_(Schematics).5V, Shift_Register_1.MR, Shift_Register_1.VCC, Shift_Register_2.MR, Shift_Register_2.VCC, Shift_Register_3.MR, Shift_Register_3.VCC, LCD1.VDD, R1.Pin_1, S1.Pin_1, S1.Pin_2, S2.Pin_1, S2.Pin_2, S3.Pin_1, S3.Pin_2, POT.leg1
  N14: Shift_Register_1.Q1, R6.Pin_0
  N15: Shift_Register_1.Q2, R7.Pin_0
  N16: Shift_Register_1.Q3, R8.Pin_0
  N17: Shift_Register_1.Q4, R9.Pin_0
  N18: Shift_Register_1.Q5, R10.Pin_0
  N19: Shift_Register_1.Q6, R17.Pin_0
  N20: Shift_Register_1.Q7', Shift_Register_2.DS
  N21: Shift_Register_1.Q0, R5.Pin_0
  N22: Shift_Register_2.Q1, R12.Pin_0
  N23: Shift_Register_2.Q2, R13.Pin_0
  N24: Shift_Register_2.Q3, R14.Pin_0
  N25: Shift_Register_2.Q4, R15.Pin_0
  N26: Shift_Register_2.Q5, R16.Pin_0
  N27: Shift_Register_2.Q7', Shift_Register_3.DS
  N28: Shift_Register_2.Q0, R11.Pin_0
  N29: Shift_Register_3.Q1, R19.Pin_0
  N30: Shift_Register_3.Q2, R20.Pin_0
  N31: Shift_Register_3.Q3, R21.Pin_0
  N32: Shift_Register_3.Q4, R22.Pin_0
  N33: Shift_Register_3.Q5, R23.Pin_0
  N34: Shift_Register_3.Q0, R18.Pin_0
  N35: LCD1.V0, POT.wiper
  N36: LCD1.LED+, R1.Pin_0
  N37: LED2.anode, R6.Pin_1
  N38: LED3.anode, R7.Pin_1
  N39: LED4.anode, R8.Pin_1
  N40: LED5.anode, R9.Pin_1
  N41: LED6.anode, R10.Pin_1
  N42: LED7.anode, R11.Pin_1
  N43: LED8.anode, R12.Pin_1
  N44: LED9.anode, R13.Pin_1
  N45: LED10.anode, R14.Pin_1
  N46: LED11.anode, R15.Pin_1
  N47: LED12.anode, R16.Pin_1
  N48: LED13.anode, R17.Pin_1
  N49: LED14.anode, R18.Pin_1
  N50: LED17.anode, R21.Pin_1
  N51: LED18.anode, R22.Pin_1
  N52: LED19.anode, R23.Pin_1
  N53: R5.Pin_1, LED1.anode
  N54: R19.Pin_1, LED15.anode
  N55: LED16.anode, R20.Pin_1
  N56: J1.pin2, R24.Pin_1
